# Fritzing sketch SmartPlantCareNoSD (saved by Fritzing 0.9.3b)
breadboards: 1

parts:
  A1 = lilygo t-display-S3
  A2 = AZDelivery 2channel solid state relay module
  Part2 = FC-28 Soil Hygrometer Module - Probe
  Part3 = FC-28 Soil Hygrometer Module
  USB = DC Power [voltage=5V]
  AC = AC Power [voltage=220V frequency=60]
  Pump = Vibration Motor- ROB-08449 [package=vibe-motor-10mm]
  Power_plug1 = Power plug  # not connected

nets (from the schematic view):
  N1: A1.Pin_1, A1.Pin_2, A1.Pin_10, A1.Pin_11, A1.Pin_16, A1.Pin_18, A2.Pin_2, Part3.GND, USB.V-
  N2: A1.Pin_12, A1.Pin_28, A2.Pin_1
  N3: A1.Pin_17, Part3.VCC, USB.V+
  N4: A1.Pin_26, Part3.AO
  N5: A1.Pin_27, A2.Pin_3
  N6: A2.Pin_7, Pump.-
  N7: A2.Pin_8, AC.V-
  N8: Part2.POS, Part3.POS
  N9: Part2.NEG, Part3.NEG
  N10: AC.V+, Pump.+

custom parts:
  lilygo t-display-S3: T-Display-S3 ESP32-S3 1.9 inch ST7789 LCD Display Development Board WIFI Bluetooth5.0 Wireless Module 170*320 Resolution.
  AZDelivery 2channel solid state relay module: AZDelivery 2channel solid state relay module.
  FC-28 Soil Hygrometer Module - Probe: The FC-28 is a soil hygrometer module that uses the Texas Instruments LM393 comparator chip to provide an analog measurement of soil humidity.
  FC-28 Soil Hygrometer Module: The FC-28 is a soil hygrometer module that uses the Texas Instruments LM393 comparator chip to provide an analog measurement of soil humidity. The digital output is high when soil moisture is over a certain threshold, as determined by adjusting the potentiometer.
